# Fritzing sketch ras_pi.setup (saved by Fritzing 0.9.3b)
breadboards: 1

parts:
  Raspberry_Pi_1 = Raspberry Pi 3 [part_number=RPI-3-V1.2]
  Part1 = Adafruit ADS1115 16Bit I2C ADC [part_number="Adafruit #1085"]
  Part2 = MQ-9 breakout
  LED1 = DUO LED RG [package="5 mm [THT]"]
  Q1 = NPN-Transistor [package="TO92 [THT]"]
  Q2 = NPN-Transistor [package="TO92 [THT]"]
  R1 = Resistor [tolerance=±5% resistance=220 package="2010 [SMD]"]
  LED2 = smd LED [color="Blue (470nm)" package="0603 [SMD]"]
  S1 = Toggle Switch [package=THT]

nets:
  3V3: Raspberry_Pi_1.3v3, Part1.VDD, S1.L2
  N1: Raspberry_Pi_1.GPIO2, Part1.SDA
  N2: Raspberry_Pi_1.GPIO3, Part1.SCL
  N3: Raspberry_Pi_1.GIPO24, LED2.anode
  N4: Raspberry_Pi_1.GIPO23, S1.COM
  N5: Raspberry_Pi_1.GIPO18, Q2.B
  N6: Raspberry_Pi_1.GIPO15, Q1.B
  GND: Raspberry_Pi_1.GND, Part1.GND, Part2.GND, Q1.C, Q2.E, LED2.cathode
  5V: Raspberry_Pi_1.5V, Part2.VCC, R1.Pin_0
  N7: Part1.AIN0, Part2.AO
  N8: LED1.red_anode, Q1.E
  N9: LED1.common_cathode, R1.Pin_1
  N10: LED1.green_anode, Q2.C

custom parts:
  Adafruit ADS1115 16Bit I2C ADC: For microcontrollers without an analog-to-digital converter or when you want a higher-precision ADC, the ADS1115 provides 16-bit precision at 860 samples/second over I2C. The chip can be configured as 4 single-ended input channels, or two differential channels. As a nice bonus, it even includes a programmable gain amplifier, up to x16, to help boost up smaller single/differential signals to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
  MQ-9 breakout: SKU: 101284
